# Fritzing sketch CircuitFullColorLED (saved by Fritzing 0.9.2b)
breadboards: 1

parts:
  パーツ1 = Arduino Uno (Rev3)
  R1 = Resistor [tolerance=±5% resistance=220 package=THT]
  LED1 = RGB LED (com. cathode, rgb) [package="5 mm [THT]"]

nets:
  N1: パーツ1.D13/SCK, LED1.green_anode
  N2: パーツ1.D3_PWM, R1.Pin_1
  N3: パーツ1.D5_PWM, LED1.common_cathode
  N4: パーツ1.D6_PWM, LED1.red_anode
  N5: R1.Pin_0, LED1.blue_anode
